# Fritzing sketch Arduino kredsløbsdiagram med Power supply (saved by Fritzing 0.9.3b)
breadboards: 1
perfboards: 1

parts:
  Part1 = Arduino Mega 2560 (Rev3)
  Part2 = Thumb Joystick
  Part3 = Thumb Joystick
  LCD1 = LCD screen
  U1 = POT [package=alps_pot]
  SG1 = Buzzer 12mm [package=buzzer-12mm-ns]
  Part4 = MicroSD Card Module
  Power_plug1 = Power plug
  S1 = Toggle Switch [package=THT]
  J1 = Camdenboss CTB0158-3 [part_number=CTB0158-3 package=THT]
  J2 = Camdenboss CTB0158-3 [part_number=CTB0158-3 package=THT]
  J3 = Camdenboss CTB0158-2 [part_number=CTB0158-2 package=THT]
  C1 = Capacitor Polarized [package=cpol-radial-10uf-25v]
  Part5 = ws2812b [package="smd 2812b"]
  Part6 = ws2812b [package="smd 2812b"]

nets:
  N1: Part1.A1, Part2.VERT
  N2: Part1.A2, Part2.HORZ
  N3: Part1.A3, Part3.HORZ
  N4: Part1.A4, Part3.VERT
  N5: Part1.D12_PWM, LCD1.DB6
  N6: Part1.D11_PWM, LCD1.DB4
  N7: Part1.D2_PWM, Part2.SEL
  N8: Part1.D3_PWM, Part3.SEL
  N9: Part1.D37, SG1.2
  N10: Part1.D40, LCD1.E
  N11: Part1.D41, LCD1.R/W
  N12: Part1.D42, LCD1.RS
  N13: Part1.D43, LCD1.V0
  N14: Part1.D50, Part4.MISO
  N15: Part1.D51, Part4.MOSI
  N16: Part1.D52, Part4.SCK
  N17: Part1.D53, Part4.CS
  VCC: Part2.VCC, LCD1.LED+, U1.E, Part4.VCC
  GND: Part3.GND, LCD1.DB5, U1.A, SG1.1, Part4.GND
  N18: LCD1.DB7, U1.S
  VDD: Power_plug1.VCC, J1.pin3, J3.pin2, C1.+, Part5.VDD, Part6.VDD
  N19: S1.COM, J1.terminal_3
  N20: S1.L2, J2.pin3
  N21: J1.pin1, J2.pin1
  N22: J1.pin2, J2.pin2
  VSS: J1.terminal_1, J3.pin1, C1.-, Part5.VSS, Part6.VSS
  N23: J1.terminal_2, Part5.DIN
  N24: Part5.DOUT, Part6.DIN

notes:
  Player2
  Player1
  Fra venstre mod højre:
  CS,SCK,MOSI,MISO,VCC,GND
  WS2812B
  in a 8x8
  daisy chain configuration
  From left to right:
  GND,DATA,5V
  going to the arduino:
  GND -> GND; DATA -> pin 8; 5V -> 5V (NOT Vin!)
  From left to right:
  GND,DATA,5V
  going from the LED Matrix to the board
  1000 uF capacitor
  Switch for changing between the USB or this Power supply to run the Arduino.
  5V in which can deliver atleast 3A!
