# Fritzing sketch Arduino kredsløbsdiagram med RPI (saved by Fritzing 0.9.3b)
breadboards: 1

parts:
  Part1 = Arduino Mega 2560 (Rev3)
  Part2 = Thumb Joystick
  Part3 = Thumb Joystick
  LCD1 = LCD screen
  U1 = POT [package=alps_pot]
  SG1 = Buzzer 12mm [package=buzzer-12mm-ns]
  Part4 = MicroSD Card Module
  Part5 = Logic Level Converter
  Raspberry_Pi_1 = Raspberry Pi 3 [part_number=RPI-3-V1.2]

nets:
  N1: Part1.A1, Part2.VERT
  N2: Part1.A2, Part2.HORZ
  N3: Part1.A3, Part3.HORZ
  N4: Part1.A4, Part3.VERT
  N5: Part1.D21/SCL, Part5.GND, Raspberry_Pi_1.GPIO3
  N6: Part1.D20/SDA, Part5.HV
  N7: Part1.D12_PWM, LCD1.DB6
  N8: Part1.D11_PWM, LCD1.DB4
  N9: Part1.D2_PWM, Part2.SEL
  N10: Part1.D3_PWM, Part3.SEL
  N11: Part1.D22, Part5.TX2_HV
  N12: Part1.D37, SG1.2
  N13: Part1.D40, LCD1.E
  N14: Part1.D41, LCD1.R/W
  N15: Part1.D42, LCD1.RS
  N16: Part1.D43, LCD1.V0
  N17: Part1.D50, Part4.MISO
  N18: Part1.D51, Part4.MOSI
  N19: Part1.D52, Part4.SCK
  N20: Part1.D53, Part4.CS
  VCC: Part2.VCC, LCD1.LED+, U1.E, Part4.VCC, Part5.TX_HV
  GND: Part3.GND, LCD1.DB5, U1.A, SG1.1, Part4.GND, Part5.RX_HV
  N21: LCD1.DB7, U1.S
  N22: Part5.TX2_LV, Raspberry_Pi_1.GIPO21
  N23: Part5.LV, Raspberry_Pi_1.GPIO2
  N24: Part5.RX_LV, Raspberry_Pi_1.5V
  N25: Part5.TX_LV, Raspberry_Pi_1.3v3

notes:
  Player2
  Player1
  Fra venstre mod højre:
  CS,SCK,MOSI,MISO,VCC,GND
  , GND ,EN
  VCC, ,Data,Clock,
