# Fritzing sketch Arduino kredsløbsdiagram (saved by Fritzing 0.9.3b)
breadboards: 1

parts:
  Part1 = Arduino Mega 2560 (Rev3)
  Part2 = Thumb Joystick
  Part3 = Thumb Joystick
  LCD1 = LCD screen
  U1 = POT [package=alps_pot]
  SG1 = Buzzer 12mm [package=buzzer-12mm-ns]
  Part4 = MicroSD Card Module

nets:
  N1: Part1.A1, Part2.VERT
  N2: Part1.A2, Part2.HORZ
  N3: Part1.A3, Part3.HORZ
  N4: Part1.A4, Part3.VERT
  N5: Part1.D12_PWM, LCD1.DB6
  N6: Part1.D11_PWM, LCD1.DB4
  N7: Part1.D2_PWM, Part2.SEL
  N8: Part1.D3_PWM, Part3.SEL
  N9: Part1.D37, SG1.2
  N10: Part1.D40, LCD1.E
  N11: Part1.D41, LCD1.R/W
  N12: Part1.D42, LCD1.RS
  N13: Part1.D43, LCD1.V0
  N14: Part1.D50, Part4.MISO
  N15: Part1.D51, Part4.MOSI
  N16: Part1.D52, Part4.SCK
  N17: Part1.D53, Part4.CS
  VCC: Part2.VCC, LCD1.LED+, U1.E, Part4.VCC
  GND: Part3.GND, LCD1.DB5, U1.A, SG1.1, Part4.GND
  N18: LCD1.DB7, U1.S

notes:
  Player2
  Player1
  Fra venstre mod højre:
  CS,SCK,MOSI,MISO,VCC,GND
